// Logisim project CPU.circ as structural Verilog: 6 circuits, main circuit ROM 1
module DE0_CV (
);

  wire K0, K1, K2, K3, L0, L1, L2, L3, L4, L5, L6, L7, L8, L9, S0, S1, S2, S3, S4, S5, S6, S7, S8, S9;
  wire [3:0] HEX0, HEX1, HEX2, HEX3, HEX4, HEX5;

  Hex_Digit_Display hex_digit_display_1 (.value(HEX5));  // open: dp
  LED u_L9 (.in(L9));
  // DipSwitch #(.NSwitches(1)) S8: pin names not known; wires that end beside it: S8
  // DipSwitch #(.NSwitches(1)) S9: pin names not known; wires that end beside it: S9
  Hex_Digit_Display hex_digit_display_2 (.value(HEX4));  // open: dp
  LED u_L8 (.in(L8));
  LED u_L6 (.in(L6));
  LED u_L7 (.in(L7));
  // DipSwitch #(.NSwitches(1)) S6: pin names not known; wires that end beside it: S6
  // DipSwitch #(.NSwitches(1)) S7: pin names not known; wires that end beside it: S7
  Hex_Digit_Display hex_digit_display_3 (.value(HEX3));  // open: dp
  Hex_Digit_Display hex_digit_display_4 (.value(HEX2));  // open: dp
  LED u_L5 (.in(L5));
  LED u_L4 (.in(L4));
  LED u_L3 (.in(L3));
  // DipSwitch #(.NSwitches(1)) S3: pin names not known; wires that end beside it: S3
  // DipSwitch #(.NSwitches(1)) S5: pin names not known; wires that end beside it: S5
  // DipSwitch #(.NSwitches(1)) S4: pin names not known; wires that end beside it: S4
  Hex_Digit_Display hex_digit_display_5 (.value(HEX1));  // open: dp
  Hex_Digit_Display hex_digit_display_6 (.value(HEX0));  // open: dp
  LED u_L2 (.in(L2));
  LED u_L1 (.in(L1));
  // DipSwitch #(.NSwitches(1)) S0: pin names not known; wires that end beside it: S0
  // DipSwitch #(.NSwitches(1)) S1: pin names not known; wires that end beside it: S1
  // DipSwitch #(.NSwitches(1)) S2: pin names not known; wires that end beside it: S2
  LED u_L0 (.in(L0));
  Button u_K3 (.out(K3));
  Button u_K2 (.out(K2));
  Button u_K1 (.out(K1));
  Button u_K0 (.out(K0));
endmodule

module CPU (
  output [7:0] Entrada_1,
  output [15:0] \Saída_1 ,
  output [7:0] Entrada_2,
  output [15:0] \Saída_2 
);

  wire clock_1_out, clock_2_out;

  Contador_Sincrono_8_Bits contador_sincrono_8_bits_1 (
    .Clock(clock_1_out), .Q0(Entrada_1[0]), .Q1(Entrada_1[1]), .Q2(Entrada_1[2]), .Q3(Entrada_1[3]),
    .Q4(Entrada_1[4]), .Q5(Entrada_1[5]), .Q6(Entrada_1[6]), .Q7(Entrada_1[7]));
  Clock clock_1 (.out(clock_1_out));
  Contador_Sincrono_8_Bits contador_sincrono_8_bits_2 (
    .Clock(clock_2_out), .Q0(Entrada_2[0]), .Q1(Entrada_2[1]), .Q2(Entrada_2[2]), .Q3(Entrada_2[3]),
    .Q4(Entrada_2[4]), .Q5(Entrada_2[5]), .Q6(Entrada_2[6]), .Q7(Entrada_2[7]));
  Clock clock_2 (.out(clock_2_out));
  ROM_1 rom_1_1 (.\Barramento_de_Endereços (Entrada_1), .Barramento_de_Dados(\Saída_1 ));
  ROM_2 rom_2_1 (.\Barramento_de_Endereços (Entrada_2), .Barramento_de_Dados(\Saída_2 ));
  Hex_Digit_Display hex_digit_display_1 (.value(\Saída_1 [15:12]));  // open: dp
  Hex_Digit_Display hex_digit_display_2 (.value(\Saída_2 [15:12]));  // open: dp
  Hex_Digit_Display hex_digit_display_3 (.value(\Saída_1 [7:4]));  // open: dp
  Hex_Digit_Display hex_digit_display_4 (.value(\Saída_1 [11:8]));  // open: dp
  Hex_Digit_Display hex_digit_display_5 (.value(\Saída_2 [11:8]));  // open: dp
  Hex_Digit_Display hex_digit_display_6 (.value(\Saída_2 [7:4]));  // open: dp
  Hex_Digit_Display hex_digit_display_7 (.value(\Saída_1 [3:0]));  // open: dp
  Hex_Digit_Display hex_digit_display_8 (.value(\Saída_2 [3:0]));  // open: dp

  // Other names for the same wires on the sheet: E1[7:0] = Entrada_1; E2[7:0] = Entrada_2; S1[15:0] = \Saída_1 ;
  //   S2[15:0] = \Saída_2 
endmodule

module Contador_Sincrono_8_Bits (
  input  Clock,
  output Q0,
  output Q1,
  output Q2,
  output Q3,
  output Q4,
  output Q5,
  output Q6,
  output Q7
);

  wire and_1_out, and_2_out, and_3_out, and_4_out, and_5_out, and_6_out;

  T_Flip_Flop t_ff_1 (.clk(Clock), .T(1'b1), .Q(Q0));  // open: Qn, preset, reset
  T_Flip_Flop t_ff_2 (.clk(Clock), .T(Q0), .Q(Q1));  // open: Qn, preset, reset
  and and_1 (and_1_out, Q1, Q0);
  T_Flip_Flop t_ff_3 (.clk(Clock), .T(and_1_out), .Q(Q2));  // open: Qn, preset, reset
  and and_2 (and_2_out, Q2, and_1_out);
  T_Flip_Flop t_ff_4 (.clk(Clock), .T(and_2_out), .Q(Q3));  // open: Qn, preset, reset
  and and_3 (and_3_out, Q3, and_2_out);
  T_Flip_Flop t_ff_5 (.clk(Clock), .T(and_3_out), .Q(Q4));  // open: Qn, preset, reset
  and and_4 (and_4_out, Q4, and_3_out);
  T_Flip_Flop t_ff_6 (.clk(Clock), .T(and_4_out), .Q(Q5));  // open: Qn, preset, reset
  and and_5 (and_5_out, Q5, and_4_out);
  T_Flip_Flop t_ff_7 (.clk(Clock), .T(and_5_out), .Q(Q6));  // open: Qn, preset, reset
  and and_6 (and_6_out, Q6, and_5_out);
  T_Flip_Flop t_ff_8 (.clk(Clock), .T(and_6_out), .Q(Q7));  // open: Qn, preset, reset
endmodule

module Registrador_4_Bits (
  input  Clock,
  input  Load,
  input  D3,
  input  D2,
  input  D1,
  input  D0,
  output Q3,
  output Q2,
  output Q1,
  output Q0
);

  wire multiplexer_1_out, multiplexer_2_out;

  Multiplexer #(.enable("false")) multiplexer_1 (.in0(Q3), .in1(D3), .out(multiplexer_1_out), .sel(Load));
  D_Flip_Flop d_ff_1 (.clk(Clock), .D(multiplexer_1_out), .Q(Q3));  // open: Qn, preset, reset
  Multiplexer #(.enable("false")) multiplexer_2 (.in0(Q2), .in1(D2), .out(multiplexer_2_out), .sel(Load));
  D_Flip_Flop d_ff_2 (.clk(Clock), .D(multiplexer_2_out), .Q(Q2));  // open: Qn, preset, reset
  Multiplexer #(.enable("false")) multiplexer_3 (.in0(Q1), .in1(D1), .sel(Load));  // open: out
  D_Flip_Flop d_ff_3 (.clk(Clock), .Q(Q1));  // open: D, Qn, preset, reset
  Multiplexer #(.enable("false")) multiplexer_4 (.in0(Q0), .in1(D0), .sel(Load));  // open: out
  D_Flip_Flop d_ff_4 (.clk(Clock), .Q(Q0));  // open: D, Qn, preset, reset
endmodule

module ROM_1 (
  input  [7:0] \Barramento_de_Endereços ,
  output [15:0] Barramento_de_Dados
);

  ROM #(.dataWidth(16), .Select("low")) \Memória_1  (
    .addr(\Barramento_de_Endereços ), .data(Barramento_de_Dados), .sel(1'b0));

  // Notes on the sheet:
  //   contents of Memória_1 (hex, n*v repeats v):
  //   6005 9101 6202 6304 c08 0 0 0 400 6001 9001 9002 6302 6102 9302 6200 6001 800
endmodule

module ROM_2 (
  input  [7:0] \Barramento_de_Endereços ,
  output [15:0] Barramento_de_Dados
);

  ROM #(.dataWidth(16), .Select("low")) \Memória_2  (
    .addr(\Barramento_de_Endereços ), .data(Barramento_de_Dados), .sel(1'b0));

  // Notes on the sheet:
  //   contents of Memória_2 (hex, n*v repeats v):
  //   6004 9102 6201 6305 9002 6002 9003 400 c0d 4*0 9002 6302 6101 9302 6200 6003 800
endmodule
